# Fritzing sketch desenho (saved by Fritzing 0.9.3b)
breadboards: 1

parts:
  LED1 = LED - 5mm [color="Red (633nm)" package="5 mm [THT]"]
  S1 = Pushbutton [package="[THT]"]
  S2 = Pushbutton [package="[THT]"]
  R1 = Rotary Potentiometer (Large) [maximum_resistance=100kΩ package=THT]
  R2 = Resistor [tolerance=±5% resistance=330 package="0603 [SMD]"]
  Componente2 = Arduino Ethernet Shield (Rev3)

nets:
  N1: LED1.cathode, R2.Pin_1
  N2: LED1.anode, Componente2.D8
  N3: S1.Pin_1, S1.Pin_2, Componente2.PWM_D6
  N4: S1.Pin_3, S1.Pin_4
  N5: S2.Pin_1, S2.Pin_2, Componente2.D7
  N6: S2.Pin_3, S2.Pin_4, R1.leg2, R2.Pin_0, Componente2.VIN
  N7: R1.leg1, Componente2.5V
  N8: R1.wiper, Componente2.A0
